// Logisim project BBBONLY.circ as structural Verilog: 1 circuit, main circuit BBB
module BBB (
  input  _00,
  input  _01,
  input  _10,
  input  _00_2,
  input  _01_2,
  input  _10_2,
  output [7:0] bus_0
);

  wire not_1_out, or_1_out, transistor_1_out, transistor_4_out;
  wire [7:4] controlled_inverter_1_out;

  Transistor #(.\type ("n")) transistor_1 (.in(1'b0), .out(transistor_1_out), .gate(_00));
  Transistor #(.\type ("n")) transistor_2 (.in(1'b0), .out(transistor_1_out), .gate(_10));
  Transistor #(.\type ("n")) transistor_3 (.in(1'b0), .out(transistor_1_out), .gate(_01));
  Pull_Resistor #(.pull(1)) pull_resistor_1 (.node(transistor_1_out));
  or or_1 (or_1_out, transistor_4_out, transistor_1_out);
  Pull_Resistor pull_resistor_2 (.node(_00));
  Pull_Resistor pull_resistor_3 (.node(_10));
  Pull_Resistor pull_resistor_4 (.node(_01));
  not not_1 (not_1_out, or_1_out);
  assign controlled_inverter_1_out[4] = _00 ? ~_00 : 1'bz;  // Controlled_Inverter controlled_inverter_1
  assign controlled_inverter_1_out[5] = _00 ? ~_00 : 1'bz;  // Controlled_Inverter controlled_inverter_2
  assign controlled_inverter_1_out[4] = _10 ? ~_10 : 1'bz;  // Controlled_Inverter controlled_inverter_3
  assign controlled_inverter_1_out[5] = _10 ? _10 : 1'bz;  // Controlled_Buffer controlled_buffer_1
  assign controlled_inverter_1_out[4] = _01 ? _01 : 1'bz;  // Controlled_Buffer controlled_buffer_2
  assign controlled_inverter_1_out[6] = _00_2 ? ~_00_2 : 1'bz;  // Controlled_Inverter controlled_inverter_4
  Pull_Resistor pull_resistor_5 (.node(_00_2));
  Transistor #(.\type ("n")) transistor_4 (.in(1'b0), .out(transistor_4_out), .gate(_00_2));
  assign controlled_inverter_1_out[5] = _01 ? ~_01 : 1'bz;  // Controlled_Inverter controlled_inverter_5
  assign controlled_inverter_1_out[7] = _00_2 ? ~_00_2 : 1'bz;  // Controlled_Inverter controlled_inverter_6
  assign controlled_inverter_1_out[6] = _10_2 ? ~_10_2 : 1'bz;  // Controlled_Inverter controlled_inverter_7
  assign controlled_inverter_1_out[7] = _10_2 ? _10_2 : 1'bz;  // Controlled_Buffer controlled_buffer_3
  Transistor #(.\type ("n")) transistor_5 (.in(1'b0), .out(transistor_4_out), .gate(_01_2));
  assign controlled_inverter_1_out[7] = _01_2 ? ~_01_2 : 1'bz;  // Controlled_Inverter controlled_inverter_8
  Pull_Resistor pull_resistor_6 (.node(_10_2));
  assign controlled_inverter_1_out[6] = _01_2 ? _01_2 : 1'bz;  // Controlled_Buffer controlled_buffer_4
  Pull_Resistor pull_resistor_7 (.node(_01_2));
  Transistor #(.\type ("n")) transistor_6 (.in(1'b0), .out(transistor_4_out), .gate(_10_2));
  Pull_Resistor #(.pull(1)) pull_resistor_8 (.node(transistor_4_out));
  // Probe on {controlled_inverter_1_out, 4'b0000}
  Register register_1 (.D({controlled_inverter_1_out, 4'b0000}), .en(1'b1), .Q(bus_0), .clk(not_1_out));  // open: clr
endmodule
