// Logisim project CdM-8-mark5-full_30.04_всесхемы (1).circ as structural Verilog: 16 circuits, main circuit main
module CdM_8_mark5 (
  input  [7:0] data_in,
  input  [2:0] vec,
  input  IRQ,
  input  clock,
  output [7:0] r0,
  output [7:0] r2,
  output [7:0] PC,
  output [7:0] SP,
  output [7:0] PS,
  output [7:0] r1,
  output [7:0] r3,
  output [7:0] addr,
  output mem_read,
  output mem_cycle,
  output data_inst,
  output [7:0] data_out,
  output IAck
);

  wire addsp, ALU2b1, alu_1, alu_2, and_1_out, and_2_out, and_3_out, and_4_out, and_5_out, and_7_out,
       and_8_out, and_9_out, and_14_out, and_15_out, and_16_out, and_17_out, asrtD, asrtS, br_nop, br_taken,
       branch_logic_1_go, CL, cmp, crc, CUT, decoder_1_out0, decoder_1_out1, decoder_1_out2, decoder_1_out3,
       decoder_2_out0, decoder_2_out1, decoder_2_out2, decoder_2_out3, decoder_3_out3, decoder_7_out0,
       decoder_8_out0, decoder_8_out1, decoder_8_out2, decoder_8_out3, fetch, halt, inc3_1_c, ioi, jsr,
       latch, latchPC, latchPS, latchPSR, latchRX, latchSP, ldc, ldi, ldsa, m_ld, m_st, nand_1_out,
       nor_1_out, not_1_out, odd, or_1_out, or_2_out, or_3_out, or_4_out, or_5_out, or_7_out, PC2b0, PC2b1,
       PCinc, po, popall, priority_encoder_1_gs, priority_encoder_2_gs, PSR2b1, pu, pushall, register_4_q,
       register_9_q, RR2b1, rti, rts, RX2PC, setsp, SP2b0, SP2b1, SPoff2b1, SPoffset, SPstep, stop, up_down,
       vec_t, \wait ;
  wire [1:0] neg2_1_out, priority_encoder_1_out, Rd, Rs;
  wire [2:0] and_18_out, fun, inc3_1_out, multiplexer_1_out, phase, vec_addr;
  wire [3:0] alu_1_n, multiplexer_8_out, register_8_q_2;
  wire [4:0] priority_encoder_2_out;
  wire [7:0] adder_1_out, adder_2_out, alu_1_s, bus0, inc_1_out, incdec_1_out, multiplexer_2_out,
       multiplexer_6_out, multiplexer_7_out, register_11_q, register_13_q;
  wire [7:4] register_8_q;

  Decoder #(.select(2), .disabled(0), .enable("false")) decoder_1 (
    .out0(decoder_1_out0), .out1(decoder_1_out1), .out2(decoder_1_out2), .out3(decoder_1_out3), .sel(Rd));
  Register #(.width(3), .trigger("falling")) register_1 (.D(vec), .en(IAck), .Q(vec_addr), .clk(CL));  // open: clr
  or or_1 (or_1_out, \wait , stop);
  assign bus0 = decoder_2_out0 ? r0 : 8'bz;  // Controlled_Buffer controlled_buffer_1
  Register #(.trigger("falling")) register_2 (.D(data_out), .en(and_1_out), .Q(r0), .clk(CL));  // open: clr
  and and_1 (and_1_out, decoder_1_out0, latch);
  and and_2 (and_2_out, decoder_1_out0, asrtD);
  assign data_out = and_2_out ? r0 : 8'bz;  // Controlled_Buffer controlled_buffer_2
  Register #(.width(3), .trigger("falling")) register_3 (.D(multiplexer_1_out), .Q(phase), .clk(CL));  // open: en, clr
  Multiplexer #(.width(3), .enable("false")) multiplexer_1 (
    .in0(inc3_1_out), .in1(3'b000), .out(multiplexer_1_out), .sel(CUT));
  nand nand_1 (nand_1_out, IRQ, \wait );
  Register #(.width(1), .trigger("falling")) register_4 (
    .D(nand_1_out), .en(or_1_out), .Q(register_4_q), .clk(clock));  // open: clr
  assign bus0 = decoder_2_out1 ? r1 : 8'bz;  // Controlled_Buffer controlled_buffer_3
  Register #(.trigger("falling")) register_5 (.D(data_out), .en(and_3_out), .Q(r1), .clk(CL));  // open: clr
  and and_3 (and_3_out, decoder_1_out1, latch);
  and and_4 (and_4_out, decoder_1_out2, latch);
  and and_5 (and_5_out, decoder_1_out1, asrtD);
  assign data_out = and_5_out ? r1 : 8'bz;  // Controlled_Buffer controlled_buffer_4
  and and_6 (CL, ~register_4_q, clock);  // AND_Gate
  assign bus0 = decoder_2_out2 ? r2 : 8'bz;  // Controlled_Buffer controlled_buffer_5
  Register #(.trigger("falling")) register_6 (.D(data_out), .en(and_4_out), .Q(r2), .clk(CL));  // open: clr
  and and_7 (and_7_out, decoder_1_out3, latch);
  and and_8 (and_8_out, decoder_1_out2, asrtD);
  and and_9 (and_9_out, decoder_1_out3, asrtD);
  assign data_out = and_8_out ? r2 : 8'bz;  // Controlled_Buffer controlled_buffer_6
  Multiplexer #(.width(8), .enable("false")) multiplexer_2 (
    .in0(data_out), .in1(8'hd8), .out(multiplexer_2_out), .sel(IAck));
  nor nor_1 (nor_1_out, phase[0], phase[1], phase[2]);
  inc3 inc3_1 (.in(phase), .out(inc3_1_out), .C(inc3_1_c));
  or or_2 (or_2_out, inc3_1_c, CUT);
  assign bus0 = decoder_2_out3 ? r3 : 8'bz;  // Controlled_Buffer controlled_buffer_7
  Register #(.trigger("falling")) register_7 (.D(data_out), .en(and_7_out), .Q(r3), .clk(CL));  // open: clr
  assign data_out = and_9_out ? r3 : 8'bz;  // Controlled_Buffer controlled_buffer_8
  and and_10 (IAck, PS[7], fetch, IRQ);
  Register #(.trigger("falling")) register_8 (
    .D(multiplexer_2_out), .en(fetch), .Q({register_8_q, register_8_q_2}), .clk(CL));  // open: clr
  and and_11 (fetch, nor_1_out, not_1_out);
  Register #(.width(1), .trigger("falling")) register_9 (
    .D(not_1_out), .en(or_2_out), .Q(register_9_q), .clk(CL));  // open: clr
  not not_1 (not_1_out, register_9_q);
  Decoder #(.select(2), .disabled(0)) decoder_2 (
    .out0(decoder_2_out0), .out1(decoder_2_out1), .out2(decoder_2_out2), .out3(decoder_2_out3), .sel(Rs),
    .en(asrtS));
  Register #(.trigger("falling")) register_10 (.D(multiplexer_6_out), .en(or_3_out), .Q(PC), .clk(CL));  // open: clr
  or or_3 (or_3_out, latchPC, PCinc, RX2PC);
  Multiplexer #(.select(2), .width(2), .disabled(0), .enable("false")) multiplexer_3 (
    .in0(register_8_q_2[1:0]), .in1(neg2_1_out), .in2(phase[1:0]), .out(Rd), .sel({popall, pushall}));  // open: in3
  neg2 neg2_1 (.inp(phase[1:0]), .out(neg2_1_out));
  assign bus0 = PC2b0 ? PC : 8'bz;  // Controlled_Buffer controlled_buffer_9
  inc inc_1 (.in(PC), .out(inc_1_out), .\disable (IAck));
  Register #(.trigger("falling")) register_11 (.D(data_out), .en(latchRX), .Q(register_11_q), .clk(CL));  // open: clr
  assign data_out = PC2b1 ? PC : 8'bz;  // Controlled_Buffer controlled_buffer_10
  Multiplexer #(.width(2), .disabled(0), .enable("false")) multiplexer_4 (
    .in0(register_8_q_2[3:2]), .in1(register_8_q_2[1:0]), .out(Rs), .sel(or_4_out));
  Multiplexer #(.width(3), .enable("false")) multiplexer_5 (
    .in0(register_8_q[6:4]), .in1({register_8_q[4], register_8_q_2[3:2]}), .out(fun), .sel(alu_1));
  Multiplexer #(.select(2), .width(8), .enable("false")) multiplexer_6 (
    .in0(data_out), .in1(inc_1_out), .in2(register_11_q), .out(multiplexer_6_out), .sel({RX2PC, PCinc}));  // open: in3
  or or_4 (or_4_out, alu_1, ldsa);
  and and_12 (cmp, ~register_8_q[7], register_8_q[6], register_8_q[5], register_8_q[4]);  // AND_Gate
  and and_13 (alu_1, register_8_q[7], ~register_8_q[6], ~register_8_q[5]);  // AND_Gate
  not not_2 (alu_2, register_8_q[7]);
  Decoder #(.select(2), .disabled(0)) decoder_3 (
    .out0(pu), .out1(po), .out2(ldsa), .out3(decoder_3_out3), .sel(register_8_q_2[3:2]), .en(and_14_out));
  and and_14 (and_14_out, register_8_q[7], register_8_q[6], ~register_8_q[5], ~register_8_q[4]);  // AND_Gate
  and and_15 (and_15_out, register_8_q[7], ~register_8_q[6], register_8_q[5]);  // AND_Gate
  Decoder #(.disabled(0)) decoder_4 (.out0(m_st), .out1(m_ld), .sel(register_8_q[4]), .en(and_15_out));
  or or_5 (or_5_out, latchSP, SPstep, SPoffset);
  Decoder #(.select(2), .disabled(0)) decoder_5 (
    .out0(addsp), .out1(setsp), .out2(pushall), .out3(popall), .sel(register_8_q_2[1:0]), .en(decoder_3_out3));
  and and_16 (and_16_out, register_8_q[5], register_8_q[6], register_8_q[7]);
  Decoder #(.disabled(0)) decoder_6 (.out0(br_nop), .out1(br_taken), .sel(branch_logic_1_go), .en(decoder_7_out0));
  assign bus0 = SP2b0 ? SP : 8'bz;  // Controlled_Buffer controlled_buffer_11
  Register #(.trigger("falling")) register_12 (.D(multiplexer_7_out), .en(or_5_out), .Q(SP), .clk(CL));  // open: clr
  assign data_out = SP2b1 ? SP : 8'bz;  // Controlled_Buffer controlled_buffer_12
  and and_17 (and_17_out, register_8_q[7], register_8_q[6], ~register_8_q[5], register_8_q[4]);  // AND_Gate
  Decoder #(.disabled(0)) decoder_7 (.out0(decoder_7_out0), .out1(ldc), .sel(register_8_q[4]), .en(and_16_out));
  branch_logic branch_logic_1 (.cccc(register_8_q_2), .CVZN(PS[3:0]), .go(branch_logic_1_go));
  Adder adder_1 (.a(bus0), .b(SP), .out(adder_1_out));  // open: cin, cout
  assign data_out = SPoff2b1 ? adder_1_out : 8'bz;  // Controlled_Buffer controlled_buffer_13
  Decoder #(.select(4), .disabled(0)) decoder_8 (
    .out0(decoder_8_out0), .out1(decoder_8_out1), .out2(decoder_8_out2), .out3(decoder_8_out3), .out4(halt),
    .out5(\wait ), .out6(jsr), .out7(rts), .out8(ioi), .out9(rti), .out10(crc), .sel(register_8_q_2),
    .en(and_17_out));  // open: out11, out12, out13, out14, out15
  incdec incdec_1 (.in(SP), .out(incdec_1_out), .up_down(up_down));
  Adder adder_2 (.a(SP), .b(data_out), .out(adder_2_out));  // open: cin, cout
  or or_6 (ldi, decoder_8_out0, decoder_8_out1, decoder_8_out2, decoder_8_out3);
  Multiplexer #(.select(2), .width(8), .enable("false")) multiplexer_7 (
    .in0(data_out), .in1(incdec_1_out), .in2(adder_2_out), .out(multiplexer_7_out), .sel({SPoffset, SPstep}));  // open: in3
  ALU u_alu_1 (
    .C_in(PS[3]), .N(alu_1_n[0]), .\function ({alu_1, fun}), .A(bus0), .B(data_out), .Z(alu_1_n[1]),
    .S(alu_1_s), .C(alu_1_n[3]), .V(alu_1_n[2]));
  assign data_out = ALU2b1 ? alu_1_s : 8'bz;  // Controlled_Buffer controlled_buffer_14
  Register #(.trigger("falling")) register_13 (.D(alu_1_s), .en(1'b1), .Q(register_13_q), .clk(CL));  // open: clr
  assign data_out = RR2b1 ? register_13_q : 8'bz;  // Controlled_Buffer controlled_buffer_15
  Priority_Encoder #(.select(2), .disabled(0)) priority_encoder_1 (
    .in0(pushall), .in1(popall), .in2(ioi), .in3(fetch), .out(priority_encoder_1_out),
    .gs(priority_encoder_1_gs));  // open: en_out, en_in
  Priority_Encoder #(.select(5), .disabled(0)) priority_encoder_2 (
    .in0(alu_2), .in1(cmp), .in2(alu_1), .in3(m_ld), .in4(m_st), .in5(ldc), .in6(ldi), .in7(setsp),
    .in8(addsp), .in9(pu), .in10(po), .in11(ldsa), .in12(br_nop), .in13(br_taken), .in14(jsr), .in15(rts),
    .in16(crc), .in17(rti), .in18(\wait ), .in19(halt), .in20(fetch), .in21(1'b0), .in22(1'b0), .in23(1'b0),
    .in24(1'b0), .in25(1'b0), .in26(1'b0), .in27(1'b0), .in28(1'b0), .in29(1'b0), .in30(1'b0), .in31(1'b0),
    .out(priority_encoder_2_out), .gs(priority_encoder_2_gs));  // open: en_out, en_in
  Multiplexer #(.width(4), .enable("false")) multiplexer_8 (
    .in0(data_out[3:0]), .in1(alu_1_n), .out(multiplexer_8_out), .sel(latchPS));
  or or_7 (or_7_out, latchPS, latchPSR);
  Register #(.width(4), .trigger("falling")) register_14 (
    .D(multiplexer_8_out), .en(or_7_out), .Q(PS[3:0]), .clk(CL));  // open: clr
  Register #(.width(4), .trigger("falling")) register_15 (
    .D(data_out[7:4]), .en(latchPSR), .Q(PS[7:4]), .clk(CL));  // open: clr
  // Probe on data_out
  assign data_out = PSR2b1 ? PS : 8'bz;  // Controlled_Buffer controlled_buffer_16
  assign data_out = mem_read ? data_in : 8'bz;  // Controlled_Buffer controlled_buffer_17
  // Probe on data_in
  ROM #(.addrWidth(5), .dataWidth(28)) rom_1 (
    .addr({phase, priority_encoder_1_out}),
    .data({CUT, vec_t, up_down, stop, odd, mem_read, mem_cycle, latchSP, latchRX, latchPSR, latchPS, latchPC, latch, data_inst, asrtS, asrtD, SPstep, SPoffset, SPoff2b1, SP2b1, SP2b0, RX2PC, RR2b1, PSR2b1, PCinc, PC2b1, PC2b0, ALU2b1}),
    .sel(priority_encoder_1_gs));
  ROM #(.addrWidth(6), .dataWidth(28)) rom_2 (
    .addr({phase[0], priority_encoder_2_out}),
    .data({CUT, vec_t, up_down, stop, odd, mem_read, mem_cycle, latchSP, latchRX, latchPSR, latchPS, latchPC, latch, data_inst, asrtS, asrtD, SPstep, SPoffset, SPoff2b1, SP2b1, SP2b0, RX2PC, RR2b1, PSR2b1, PCinc, PC2b1, PC2b0, ALU2b1}),
    .sel(priority_encoder_2_gs));
  Pull_Resistor pull_resistor_1 (.node(bus0[7]));
  Pull_Resistor pull_resistor_2 (.node(bus0[6]));
  assign and_18_out = {3{vec_t}} & vec_addr;  // AND_Gate and_18, 3 bits wide
  Pull_Resistor pull_resistor_3 (.node(bus0[4]));
  Pull_Resistor pull_resistor_4 (.node(bus0[0]));
  Pull_Resistor pull_resistor_5 (.node(bus0[3]));
  Pull_Resistor pull_resistor_6 (.node(bus0[2]));
  Pull_Resistor pull_resistor_7 (.node(bus0[1]));
  Pull_Resistor pull_resistor_8 (.node(bus0[5]));
  Multiplexer #(.width(8), .enable("false")) multiplexer_9 (
    .in0(bus0), .in1({4'b1111, and_18_out, odd}), .out(addr), .sel(vec_t));
  // NOT_Gate not_3 is placed but not wired

  // Other names for the same wires on the sheet: bus1[7:0] = data_out; data = data_inst; mem = mem_cycle;
  //   mem_ld = mem_read; fun[3] = alu_1; PCnoInc = IAck; CVZN[3:0] = PS[3:0]; PSR[7:0] = PS

  // Notes on the sheet:
  //   destination
  //   r0
  //   8-phase Sequencer with int.
  //   Seq
  //   r2
  //   r1
  //   r3
  //   source
  //   IR
  //   fetch toggle
  //   instruction
  //   RX
  //   Coco de Mer 8 (CdM-8) Mark 5
  //   Primary
  //   decoder
  //   ALU
  //   RR
  //   PS
  //   Secondary
  //   decoder
  //   contents of rom_1 (hex, n*v repeats v):
  //   800 260d880 800 860000a 205880 260d880 204884 0 205880 260d880 204090 0 205880 a60d880 4610000 0
  //   8205080 0 ce40000
  //   contents of rom_2 (hex, n*v repeats v):
  //   23000 8023000 802a001 860e000 8207000 860a000 860800a 870000a 870040a 800 a60c880 60800a 8000008
  //   8610002 68080a a614880 684080 2644880 0 9000000 860000a 11*0 8008020 8*0 8205080 0 800a200 0 0
  //   82140c4 0 82140c4 a614880
endmodule

module inc (
  input  \disable ,
  input  [7:0] in,
  output [7:0] out
);

  wire [7:0] not_1_out;
  wire [7:7] and_1_out;

  // Probe on in
  assign {and_1_out[7], not_1_out[7:1]} = in & not_1_out;  // AND_Gate and_1, 8 bits wide
  assign out = not_1_out ^ in;  // XOR_Gate xor_1, 8 bits wide
  Pull_Resistor pull_resistor_1 (.node(\disable ));
  not not_1 (not_1_out[0], \disable );
  // Probe on out

  // Notes on the sheet:
  //   x
  //   x
  //   +1
endmodule

module incdec (
  input  [7:0] in,
  input  up_down,
  output [7:0] out
);

  wire [7:0] and_1_out, or_1_out, xnor_1_out, xor_1_out;

  // Probe on in
  assign or_1_out = in | {or_1_out[6:0], 1'b0};  // OR_Gate or_1, 8 bits wide
  assign xnor_1_out = ~({or_1_out[6:0], 1'b0} ^ in);  // XNOR_Gate xnor_1, 8 bits wide
  assign and_1_out = in & {and_1_out[6:0], 1'b1};  // AND_Gate and_1, 8 bits wide
  assign xor_1_out = {and_1_out[6:0], 1'b1} ^ in;  // XOR_Gate xor_1, 8 bits wide
  // Probe on xnor_1_out
  // Probe on xor_1_out
  Multiplexer #(.width(8), .enable("false")) multiplexer_1 (
    .in0(xnor_1_out), .in1(xor_1_out), .out(out), .sel(up_down));

  // Notes on the sheet:
  //   x
  //   x
  //   –1
  //   x
  //   +1
endmodule

module ALU (
  input  C_in,
  input  [3:0] \function ,
  input  [7:0] A,
  input  [7:0] B,
  output N,
  output Z,
  output [7:0] S,
  output C,
  output V
);

  wire adder_v_1_c_out, adder_v_1_v, adder_v_2_c_out, adder_v_2_v, and_1_out, and_2_out, and_4_out,
       and_5_out, multiplexer_6_out, or_1_out, xor_2_out;
  wire [7:0] adder_v_1_s, adder_v_2_s, and_3_out, multiplexer_1_out, multiplexer_2_out, multiplexer_5_out,
       not_1_out, or_2_out, or_3_out, xnor_1_out, xor_1_out;

  Pull_Resistor pull_resistor_1 (.node(A[0]));
  Pull_Resistor pull_resistor_2 (.node(A[1]));
  Pull_Resistor pull_resistor_3 (.node(A[2]));
  Pull_Resistor pull_resistor_4 (.node(A[3]));
  Pull_Resistor pull_resistor_5 (.node(A[4]));
  Pull_Resistor pull_resistor_6 (.node(A[5]));
  Pull_Resistor pull_resistor_7 (.node(A[6]));
  Pull_Resistor pull_resistor_8 (.node(A[7]));
  // Probe on A
  Pull_Resistor pull_resistor_9 (.node(B[0]));
  Pull_Resistor pull_resistor_10 (.node(B[1]));
  Pull_Resistor pull_resistor_11 (.node(B[2]));
  Pull_Resistor pull_resistor_12 (.node(B[3]));
  Pull_Resistor pull_resistor_13 (.node(B[4]));
  Pull_Resistor pull_resistor_14 (.node(B[5]));
  Pull_Resistor pull_resistor_15 (.node(B[6]));
  Pull_Resistor pull_resistor_16 (.node(B[7]));
  // Probe on B
  assign not_1_out = ~B;  // NOT_Gate not_1, 8 bits wide
  and and_1 (and_1_out, \function [1], ~\function [0], C_in);  // AND_Gate
  or or_1 (or_1_out, and_1_out, and_2_out);
  Multiplexer #(.select(2), .width(8), .enable("false")) multiplexer_1 (
    .in0({8{1'b0}}), .in1(B), .in2(B), .in3(not_1_out), .out(multiplexer_1_out), .sel(\function [1:0]));
  and and_2 (and_2_out, \function [1], \function [0]);
  adder_V adder_v_1 (
    .A(A), .B(multiplexer_1_out), .S(adder_v_1_s), .C_in(or_1_out), .C_out(adder_v_1_c_out), .V(adder_v_1_v));
  assign and_3_out = A & B;  // AND_Gate and_3, 8 bits wide
  assign or_2_out = A | B;  // OR_Gate or_2, 8 bits wide
  and and_4 (and_4_out, \function [0], \function [1], adder_v_1_v);
  Multiplexer #(.select(2), .width(8), .enable("false")) multiplexer_2 (
    .in0(and_3_out), .in1(or_2_out), .in2(xor_1_out), .in3(adder_v_1_s), .out(multiplexer_2_out),
    .sel(\function [1:0]));
  assign xor_1_out = A ^ B;  // XOR_Gate xor_1, 8 bits wide
  or or_3 (or_3_out[0], \function [0], \function [1]);
  and dec (or_3_out[7], ~\function [0], \function [1]);  // AND_Gate
  Multiplexer #(.select(2), .enable("false")) multiplexer_3 (
    .in0(adder_v_1_c_out), .in1(1'b0), .in2(adder_v_2_c_out), .in3(multiplexer_6_out), .out(C),
    .sel(\function [3:2]));
  Multiplexer #(.select(2), .enable("false")) multiplexer_4 (
    .in0(adder_v_1_v), .in1(and_4_out), .in2(adder_v_2_v), .in3(and_5_out), .out(V), .sel(\function [3:2]));
  assign xnor_1_out = ~({8{\function [1]}} ^ A);  // XNOR_Gate xnor_1, 8 bits wide
  adder_V adder_v_2 (
    .A({{7{or_3_out[7]}}, or_3_out[0]}), .B(xnor_1_out), .S(adder_v_2_s), .C_in(1'b0),
    .C_out(adder_v_2_c_out), .V(adder_v_2_v));
  Multiplexer #(.select(2), .width(8), .enable("false")) multiplexer_5 (
    .in0({C_in, A[7:1]}), .in1({A[6:0], 1'b0}), .in2({{2{A[7]}}, A[6:1]}), .in3({A[3:0], A[7:4]}),
    .out(multiplexer_5_out), .sel(\function [1:0]));
  Multiplexer #(.select(2), .enable("false")) multiplexer_6 (
    .in0(A[0]), .in1(A[7]), .in2(A[0]), .in3(1'b0), .out(multiplexer_6_out), .sel(\function [1:0]));
  // Probe on {N, S[6:0]}
  Multiplexer #(.select(2), .width(8), .enable("false")) multiplexer_7 (
    .in0(adder_v_1_s), .in1(multiplexer_2_out), .in2(adder_v_2_s), .in3(multiplexer_5_out),
    .out({N, S[6:0]}), .sel(\function [3:2]));
  xor xor_2 (xor_2_out, A[7], A[6]);
  nor nor_1 (Z, S[0], S[1], S[2], S[3], S[4], S[5], S[6], N);
  and and_5 (and_5_out, \function [0], ~\function [1], xor_2_out);  // AND_Gate

  assign S[7] = N;

  // Notes on the sheet:
  //   to avoid undriven input to arith. devices
  //   to avoid undriven input to arith. devices
  //   move
  //   add
  //   addc
  //   sub
  //   addc
  //   sub/cmp
  //   cmp
  //   and
  //   or
  //   xor
  //   cmp
  //   not/neg
  //   dec/inc/neg
  //   shr
  //   shla
  //   shra
  //   swan
endmodule

module adder_V (
  input  C_in,
  input  [7:0] A,
  input  [7:0] B,
  output [7:0] S,
  output C_out,
  output V
);

  wire [7:0] and_1_out, and_2_out, and_3_out;
  wire [7:1] or_1_out;

  // Probe on A
  // Probe on B
  assign S = A ^ {or_1_out, C_in} ^ B;  // XOR_Gate xor_1, 8 bits wide
  assign and_1_out = B & A;  // AND_Gate and_1, 8 bits wide
  assign and_2_out = B & {or_1_out, C_in};  // AND_Gate and_2, 8 bits wide
  assign and_3_out = A & {or_1_out, C_in};  // AND_Gate and_3, 8 bits wide
  assign {C_out, or_1_out} = and_1_out | and_2_out | and_3_out;  // OR_Gate or_1, 8 bits wide
  // Probe on S
  xor xor_2 (V, or_1_out[7], C_out);
endmodule

module branch_logic (
  input  [3:0] cccc,
  input  [3:0] CVZN,
  output go
);

  wire and_1_out, and_2_out, and_3_out, and_4_out, and_5_out, and_6_out, and_7_out, decoder_1_out0,
       decoder_1_out1, decoder_1_out2, decoder_1_out3, decoder_2_out0, decoder_2_out1, decoder_2_out2,
       decoder_2_out3, not_1_out, not_2_out, or_1_out, xnor_1_out;

  not not_1 (not_1_out, cccc[3]);
  Decoder #(.select(2), .disabled(0)) decoder_1 (
    .out0(decoder_1_out0), .out1(decoder_1_out1), .out2(decoder_1_out2), .out3(decoder_1_out3),
    .sel(cccc[2:1]), .en(not_1_out));
  and and_1 (and_1_out, decoder_1_out0, CVZN[1]);
  and and_2 (and_2_out, decoder_1_out1, CVZN[3]);
  and and_3 (and_3_out, decoder_1_out2, CVZN[0]);
  and and_4 (and_4_out, decoder_1_out3, CVZN[2]);
  not not_2 (not_2_out, CVZN[1]);
  xnor xnor_1 (xnor_1_out, CVZN[0], CVZN[2]);
  Decoder #(.select(2), .disabled(0)) decoder_2 (
    .out0(decoder_2_out0), .out1(decoder_2_out1), .out2(decoder_2_out2), .out3(decoder_2_out3),
    .sel(cccc[2:1]), .en(cccc[3]));
  and and_5 (and_5_out, decoder_2_out0, not_2_out, CVZN[3]);
  and and_6 (and_6_out, xnor_1_out, decoder_2_out1);
  and and_7 (and_7_out, not_2_out, xnor_1_out, decoder_2_out2);
  or or_1 (or_1_out, and_1_out, and_2_out, and_3_out, and_4_out, and_5_out, and_6_out, and_7_out, decoder_2_out3);
  xor xor_1 (go, cccc[0], or_1_out);

  // Notes on the sheet:
  //   N
  //   Z
  //   V
  //   C
  //   EQ
  //   HS/CS
  //   MI
  //   VS
  //   N=V
  //   Z'
  //   HI
  //   GE
  //   GT
  //   <always>
endmodule

module inc3 (
  input  [2:0] in,
  output [2:0] out,
  output C
);

  wire [2:1] and_1_out;

  // Probe on in
  assign {C, and_1_out} = in & {and_1_out, 1'b1};  // AND_Gate and_1, 3 bits wide
  assign out = {and_1_out, 1'b1} ^ in;  // XOR_Gate xor_1, 3 bits wide
  // Probe on out

  // Notes on the sheet:
  //   x
  //   x
  //   +1
endmodule

module neg2 (
  input  [1:0] inp,
  output [1:0] out
);

  wire [1:0] not_1_out;

  assign not_1_out = ~inp;  // NOT_Gate not_1, 2 bits wide
  not not_2 (out[0], not_1_out[0]);
  xor xor_1 (out[1], not_1_out[0], not_1_out[1]);
endmodule

module test (
);

  wire and_2_out, and_3_out, and_4_out, arbiter_1_vec, cdm_8_mark5_1_data_inst, cdm_8_mark5_1_mem_cycle, clk,
       decoder_1_out0, decoder_1_out1, decoder_2_out0, decoder_2_out1, decoder_2_out2, decoder_2_out3, IAck,
       IOsel, IRQ, not_1_out, not_2_out, READwrite;
  wire [2:0] vec;
  wire [3:0] IOaddr;
  wire [6:0] bit_extender_1_out, keyboard_1_data;
  wire [7:0] bit_extender_2_out, cdm_8_mark5_1_data_out, cdm_8_mark5_1_pc, cdm_8_mark5_1_ps,
       cdm_8_mark5_1_r0, cdm_8_mark5_1_r1, cdm_8_mark5_1_r2, cdm_8_mark5_1_r3, cdm_8_mark5_1_sp,
       controlled_buffer_2_out, IOdat, register_1_q;
  wire [7:4] cdm_8_mark5_1_addr;

  Clock clock_1 (.out(clk));
  // Probe on cdm_8_mark5_1_r3
  // Probe on cdm_8_mark5_1_r2
  // Probe on cdm_8_mark5_1_r1
  // Probe on cdm_8_mark5_1_r0
  // Probe on cdm_8_mark5_1_pc
  and and_1 (IOsel, cdm_8_mark5_1_addr[4], cdm_8_mark5_1_addr[5], cdm_8_mark5_1_addr[6], cdm_8_mark5_1_addr[7], decoder_1_out1);
  // Probe on cdm_8_mark5_1_sp
  // Probe on cdm_8_mark5_1_ps
  CdM_8_mark5 cdm_8_mark5_1 (
    .clock(clk), .addr({cdm_8_mark5_1_addr, IOaddr}), .mem_read(READwrite),
    .mem_cycle(cdm_8_mark5_1_mem_cycle), .data_inst(cdm_8_mark5_1_data_inst),
    .data_out(cdm_8_mark5_1_data_out), .data_in(controlled_buffer_2_out), .r0(cdm_8_mark5_1_r0),
    .r1(cdm_8_mark5_1_r1), .r2(cdm_8_mark5_1_r2), .r3(cdm_8_mark5_1_r3), .PC(cdm_8_mark5_1_pc),
    .SP(cdm_8_mark5_1_sp), .PS(cdm_8_mark5_1_ps), .IAck(IAck), .IRQ(IRQ), .vec(vec));
  Decoder #(.disabled(0)) decoder_1 (
    .out0(decoder_1_out0), .out1(decoder_1_out1), .sel(cdm_8_mark5_1_data_inst), .en(cdm_8_mark5_1_mem_cycle));
  not not_1 (not_1_out, READwrite);
  assign IOdat = not_1_out ? cdm_8_mark5_1_data_out : 8'bz;  // Controlled_Buffer controlled_buffer_1
  assign controlled_buffer_2_out = READwrite ? IOdat : 8'bz;  // Controlled_Buffer controlled_buffer_2
  // Probe on {cdm_8_mark5_1_addr, IOaddr}
  and and_2 (and_2_out, decoder_1_out1, ~IOsel);  // AND_Gate
  not not_2 (not_2_out, clk);
  // Probe on IOdat
  RAM ram_1 (
    .addr({cdm_8_mark5_1_addr, IOaddr}), .data(IOdat), .sel(and_2_out), .clk(not_2_out), .ld(READwrite));  // open: clr
  ROM rom_1 (.addr({cdm_8_mark5_1_addr, IOaddr}), .data(IOdat), .sel(decoder_1_out0));
  Bit_Extender #(.out_width(7)) bit_extender_1 (.in(IOdat), .out(bit_extender_1_out));
  TTY #(.trigger("falling")) tty_1 (.data(bit_extender_1_out), .clk(clk), .we(decoder_2_out2));  // open: clr
  assign IOdat = decoder_2_out1 ? {register_1_q[7], {6{1'b0}}, register_1_q[0]} : 8'bz;  // Controlled_Buffer controlled_buffer_3
  Register #(.width(1), .trigger("falling")) register_1 (
    .D(IOdat[0]), .en(decoder_2_out0), .Q(register_1_q[0]), .clk(clk));  // open: clr
  Keyboard #(.trigger("falling")) keyboard_1 (
    .clk(clk), .re(decoder_2_out3), .avail(register_1_q[7]), .data(keyboard_1_data));  // open: clr
  and and_3 (and_3_out, IOsel, ~IOaddr[1], ~IOaddr[2], ~IOaddr[3]);  // AND_Gate
  Decoder #(.select(2), .disabled(0)) decoder_2 (
    .out0(decoder_2_out0), .out1(decoder_2_out1), .out2(decoder_2_out2), .out3(decoder_2_out3),
    .sel({IOaddr[0], READwrite}), .en(and_3_out));
  assign IOdat = decoder_2_out3 ? bit_extender_2_out : 8'bz;  // Controlled_Buffer controlled_buffer_4
  assign bit_extender_2_out = {{1{1'b0}}, keyboard_1_data};  // Bit_Extender bit_extender_2
  assign vec = arbiter_1_vec ? 3'b010 : 3'bz;  // Controlled_Buffer controlled_buffer_5
  arbiter arbiter_1 (
    .IReq_2(IRQ), .IAck(IAck), .IReq(1'b0), .vec(arbiter_1_vec), .req(and_4_out), .done(decoder_2_out3),
    .clock(clk));  // open: IAck_2
  and and_4 (and_4_out, register_1_q[7], register_1_q[0]);

  // Notes on the sheet:
  //   contents of rom_1 (hex, n*v repeats v):
  //   cd f0 d0 0 d1 10 a4 d1 11 a4 d0 f0 d1 1 a1 c0 d0 17 c0 d0 80 c0 d9 c4 3f d0 af d6 9d d0 10 b0 d1 11
  //   b5 71 e1 29 d5 ee 1d b2 8c d1 f 44 d1 10 a4 a e0 40 d 95 95 95 97 17 d1 30 39 17 ee 55 d0 b6 d6 9d e
  //   9f d1 f 4d d6 67 d1 f 49 d6 67 d0 af d6 9d 3f ee 1d 30 31 32 33 34 35 36 37 38 39 61 62 63 64 65 66
  //   d0 57 14 f0 d1 f1 a4 d7 ce d0 f1 b2 d1 11 b5 8d d0 f 41 d0 10 b0 74 e0 97 89 d0 f 41 d0 f1 a2 d0 a
  //   78 e1 8d 3a a6 8d d0 f 41 d0 11 a1 ee 9b d0 a8 d6 9d cf d9 d1 f1 f2 8c a e0 a7 a6 ee 9f d7 77 61 69
  //   74 21 d 0 d 64 65 63 3a 20 0 68 65 78 3a 20 57*0 6f
  //   low-pri
endmodule

module arbiter (
  input  IReq,
  input  IAck,
  input  clock,
  input  req,
  input  done,
  output vec,
  output IReq_2,
  output IAck_2
);

  wire _00_out, _01_2_out, _01_out, _10_out, or_2_out;
  wire [1:0] nor_1_out, register_1_q;

  or or_1 (IReq_2, IReq, register_1_q[0]);
  and _01 (_01_out, ~register_1_q[1], register_1_q[0]);  // AND_Gate
  and and_1 (vec, _01_out, IAck);
  and and_2 (IAck_2, IAck, ~_01_out);  // AND_Gate
  and _00 (_00_out, req, ~register_1_q[0], ~register_1_q[1]);  // AND_Gate
  or or_2 (or_2_out, _00_out, _01_2_out, _10_out);
  and _01_2 (_01_2_out, IAck, register_1_q[0], ~register_1_q[1]);  // AND_Gate
  and _10 (_10_out, done, ~register_1_q[0], register_1_q[1]);  // AND_Gate
  Register #(.width(2), .trigger("falling")) register_1 (
    .D(nor_1_out), .en(or_2_out), .Q(register_1_q), .clk(clock));  // open: clr
  nor nor_1 (nor_1_out[0], register_1_q[0], register_1_q[1]);
  and and_3 (nor_1_out[1], register_1_q[0], ~register_1_q[1]);  // AND_Gate

  // Notes on the sheet:
  //   Req
  //   Ack
  //   done
  //   00: quiescence 
  //   01: IReq, waiting for Ack
  //   10: Got Ack, waiting for done
  //   0->1->2->0
endmodule

module test0 (
);

  wire _0_b_out, _1_a_out, _2_b_prime_out, and_2_out, button_1_out, cdm_8_mark5_1_data_inst,
       cdm_8_mark5_1_mem_cycle, clk, decoder_1_out0, decoder_1_out1, decoder_2_out0, decoder_2_out2, IAck,
       IO_2_out, IOsel, IRQ, not_1_out, not_2_out, or_1_out, READwrite;
  wire [1:0] nor_1_out, register_2_q;
  wire [2:0] vec;
  wire [3:0] IOaddr;
  wire [7:0] cdm_8_mark5_1_data_out, cdm_8_mark5_1_pc, cdm_8_mark5_1_ps, cdm_8_mark5_1_r0, cdm_8_mark5_1_r1,
       cdm_8_mark5_1_r2, cdm_8_mark5_1_r3, cdm_8_mark5_1_sp, controlled_buffer_2_out, IOdat, register_1_q;
  wire [7:4] cdm_8_mark5_1_addr;

  Clock clock_1 (.out(clk));
  // Probe on cdm_8_mark5_1_r3
  // Probe on cdm_8_mark5_1_r2
  // Probe on cdm_8_mark5_1_r1
  // Probe on cdm_8_mark5_1_pc
  // Probe on cdm_8_mark5_1_r0
  and and_1 (IOsel, cdm_8_mark5_1_addr[4], cdm_8_mark5_1_addr[5], cdm_8_mark5_1_addr[6], cdm_8_mark5_1_addr[7], decoder_1_out1);
  // Probe on cdm_8_mark5_1_ps
  // Probe on cdm_8_mark5_1_sp
  CdM_8_mark5 cdm_8_mark5_1 (
    .clock(clk), .addr({cdm_8_mark5_1_addr, IOaddr}), .mem_read(READwrite),
    .mem_cycle(cdm_8_mark5_1_mem_cycle), .data_inst(cdm_8_mark5_1_data_inst),
    .data_out(cdm_8_mark5_1_data_out), .data_in(controlled_buffer_2_out), .r0(cdm_8_mark5_1_r0),
    .r1(cdm_8_mark5_1_r1), .r2(cdm_8_mark5_1_r2), .r3(cdm_8_mark5_1_r3), .PC(cdm_8_mark5_1_pc),
    .SP(cdm_8_mark5_1_sp), .PS(cdm_8_mark5_1_ps), .IAck(IAck), .IRQ(IRQ), .vec(vec));
  Decoder #(.disabled(0)) decoder_1 (
    .out0(decoder_1_out0), .out1(decoder_1_out1), .sel(cdm_8_mark5_1_data_inst), .en(cdm_8_mark5_1_mem_cycle));
  not not_1 (not_1_out, READwrite);
  assign IOdat = not_1_out ? cdm_8_mark5_1_data_out : 8'bz;  // Controlled_Buffer controlled_buffer_1
  assign controlled_buffer_2_out = READwrite ? IOdat : 8'bz;  // Controlled_Buffer controlled_buffer_2
  // Probe on {cdm_8_mark5_1_addr, IOaddr}
  and and_2 (and_2_out, decoder_1_out1, ~IOsel);  // AND_Gate
  not not_2 (not_2_out, clk);
  // Probe on IOdat
  RAM ram_1 (
    .addr({cdm_8_mark5_1_addr, IOaddr}), .data(IOdat), .sel(and_2_out), .clk(not_2_out), .ld(READwrite));  // open: clr
  ROM rom_1 (.addr({cdm_8_mark5_1_addr, IOaddr}), .data(IOdat), .sel(decoder_1_out0));
  and IO_2 (IO_2_out, IOsel, ~IOaddr[0], ~IOaddr[2], ~IOaddr[3]);  // AND_Gate
  Register #(.trigger("falling")) register_1 (.D(IOdat), .en(IO_2_out), .Q(register_1_q), .clk(clk));  // open: clr
  DotMatrix #(.matrixcols(1), .matrixrows(8)) dotmatrix_1 (.col0(register_1_q));
  assign vec = IAck ? 3'b001 : 3'bz;  // Controlled_Buffer controlled_buffer_3
  Decoder #(.select(2), .enable("false")) decoder_2 (
    .out0(decoder_2_out0), .out1(IRQ), .out2(decoder_2_out2), .sel(register_2_q));  // open: out3
  Button button_1 (.out(button_1_out));
  and _0_b (_0_b_out, button_1_out, decoder_2_out0);
  and _1_a (_1_a_out, IAck, IRQ);
  and _2_b_prime (_2_b_prime_out, ~button_1_out, decoder_2_out2);  // AND_Gate
  nor nor_1 (nor_1_out[0], register_2_q[0], register_2_q[1]);
  and and_3 (nor_1_out[1], register_2_q[0], ~register_2_q[1]);  // AND_Gate
  or or_1 (or_1_out, _0_b_out, _1_a_out, _2_b_prime_out);
  Register #(.width(2), .trigger("falling")) register_2 (
    .D(nor_1_out), .en(or_1_out), .Q(register_2_q), .clk(clk));  // open: clr

  // Notes on the sheet:
  //   contents of rom_1 (hex, n*v repeats v):
  //   cd f0 d0 9 c0 d0 80 c0 d9 d3 10 d0 f2 3a a e1 14 2f ee 15 93 e3 19 d3 10 a3 ee e 82 d9 212*0 1c
  //   garland
  //   direction
  //   0->1->2->0
endmodule

module main (
  input  [7:0] \подключить_и_вводить_в_ручную ,
  input  \подключить_и_нажать_если_вводишь_в_ручную 
);

  wire button_1_out, button_2_out, button_3_out, button_4_out, button_5_out, button_6_out, button_7_out,
       button_8_out, button_9_out, cdm_8_mark5_1_data_inst, Cl, code, comparator_1_eq, comparator_2_eq, data,
       decoder_2_out0, decoder_2_out1, I_Osel, In_out_prime, IO_3_out, mem, not_1_out, or_1_out, RAM, tic_tac;
  wire [1:0] sdr_1_h0, sdr_1_h1, sdr_1_h2, sdr_1_v0, sdr_1_v1, sdr_1_v2;
  wire [2:2] tttc_1_hout, tttc_1_vout, tttc_2_vout, tttc_3_vout, tttc_4_hout, tttc_7_hout;
  wire [3:0] BPC_out_7, gsdd_1_bus_0, gsdd_1_bus_0_2, gsdd_1_bus_0_3, gsdd_1_bus_0_4, I_Oadr, tttc_1_l0,
       tttc_1_l1, tttc_1_l2, tttc_1_l3, tttc_2_l0, tttc_2_l1, tttc_2_l2, tttc_2_l3, tttc_3_l0, tttc_3_l1,
       tttc_3_l2, tttc_3_l3, tttc_4_l0, tttc_4_l1, tttc_4_l2, tttc_4_l3, tttc_5_l0, tttc_5_l1, tttc_5_l2,
       tttc_5_l3, tttc_6_l0, tttc_6_l1, tttc_6_l2, tttc_6_l3, tttc_7_l0, tttc_7_l1, tttc_7_l2, tttc_7_l3,
       tttc_8_l0, tttc_8_l1, tttc_8_l2, tttc_8_l3, tttc_9_l0, tttc_9_l1, tttc_9_l2, tttc_9_l3;
  wire [7:0] cdm_8_mark5_1_data_out, cdm_8_mark5_1_pc, cdm_8_mark5_1_ps, cdm_8_mark5_1_r0, cdm_8_mark5_1_r1,
       cdm_8_mark5_1_r2, cdm_8_mark5_1_r3, cdm_8_mark5_1_sp, controlled_buffer_2_out, I_Odat;
  wire [7:4] cdm_8_mark5_1_addr;

  and and_1 (I_Osel, or_1_out, Cl, data);
  Clock clock_1 (.out(tic_tac));
  // Probe on cdm_8_mark5_1_r0
  // Probe on cdm_8_mark5_1_r2
  // Probe on cdm_8_mark5_1_r1
  // Probe on cdm_8_mark5_1_r3
  and and_2 (RAM, ~or_1_out, data);  // AND_Gate
  // Probe on I_Odat
  DotMatrix #(.matrixcols(4), .matrixrows(4)) dotmatrix_1 (
    .col0(gsdd_1_bus_0), .col1(gsdd_1_bus_0_2), .col2(gsdd_1_bus_0_3), .col3(gsdd_1_bus_0_4));
  GSDD gsdd_1 (
    .bus_0(gsdd_1_bus_0), .bus_0_2(gsdd_1_bus_0_2), .bus_0_3(gsdd_1_bus_0_3),
    ._00___lose__10___win__11___draw(I_Odat[7:6]), .bus_0_4(gsdd_1_bus_0_4));
  // Probe on cdm_8_mark5_1_sp
  // Probe on cdm_8_mark5_1_pc
  // Probe on cdm_8_mark5_1_ps
  CdM_8_mark5 cdm_8_mark5_1 (
    .clock(tic_tac), .addr({cdm_8_mark5_1_addr, I_Oadr}), .mem_read(In_out_prime), .mem_cycle(mem),
    .data_inst(cdm_8_mark5_1_data_inst), .data_out(cdm_8_mark5_1_data_out),
    .data_in(controlled_buffer_2_out), .r0(cdm_8_mark5_1_r0), .r1(cdm_8_mark5_1_r1), .r2(cdm_8_mark5_1_r2),
    .r3(cdm_8_mark5_1_r3), .PC(cdm_8_mark5_1_pc), .SP(cdm_8_mark5_1_sp), .PS(cdm_8_mark5_1_ps));  // open: IAck, IRQ, vec
  Comparator comparator_1 (.a(8'h7), .b({cdm_8_mark5_1_addr, I_Oadr}), .eq(comparator_1_eq));  // open: gt, lt
  Comparator comparator_2 (.a(8'h3), .b({cdm_8_mark5_1_addr, I_Oadr}), .eq(comparator_2_eq));  // open: gt, lt
  SDR sdr_1 (
    .x__y(I_Odat[5:2]), .ID(I_Odat[1:0]), .h0(sdr_1_h0), .h1(sdr_1_h1), .h2(sdr_1_h2), .v2(sdr_1_v2),
    .v1(sdr_1_v1), .v0(sdr_1_v0), .clock(decoder_2_out0));
  Decoder #(.disabled(0)) decoder_1 (.out0(code), .out1(data), .sel(cdm_8_mark5_1_data_inst), .en(mem));
  assign I_Odat = not_1_out ? cdm_8_mark5_1_data_out : 8'bz;  // Controlled_Buffer controlled_buffer_1
  not not_1 (not_1_out, In_out_prime);
  assign controlled_buffer_2_out = In_out_prime ? I_Odat : 8'bz;  // Controlled_Buffer controlled_buffer_2
  or or_1 (or_1_out, comparator_2_eq, comparator_1_eq);
  Decoder #(.disabled(0)) decoder_2 (.out0(decoder_2_out0), .out1(decoder_2_out1), .sel(In_out_prime), .en(IO_3_out));
  and IO_3 (IO_3_out, I_Osel, I_Oadr[0], I_Oadr[1], ~I_Oadr[2], ~I_Oadr[3]);  // AND_Gate
  TTTC tttc_1 (
    .vin(sdr_1_h0), .vout(tttc_1_vout[2]), .hin(sdr_1_v2), .hout(tttc_1_hout[2]), .L0(tttc_1_l0),
    .L1(tttc_1_l1), .L2(tttc_1_l2), .L3(tttc_1_l3), .btn(button_1_out));
  DotMatrix #(.inputtype("row"), .matrixcols(4), .matrixrows(4)) dotmatrix_2 (
    .row0(tttc_1_l0), .row1(tttc_1_l1), .row2(tttc_1_l2), .row3(tttc_1_l3));
  Button button_1 (.out(button_1_out));
  DotMatrix #(.inputtype("row"), .matrixcols(4), .matrixrows(4)) dotmatrix_3 (
    .row0(tttc_2_l0), .row1(tttc_2_l1), .row2(tttc_2_l2), .row3(tttc_2_l3));
  TTTC tttc_2 (
    .vin(sdr_1_h1), .vout(tttc_2_vout[2]), .hin(sdr_1_v2), .hout(tttc_1_hout[2]), .L0(tttc_2_l0),
    .L1(tttc_2_l1), .L2(tttc_2_l2), .L3(tttc_2_l3), .btn(button_2_out));
  Button button_2 (.out(button_2_out));
  TTTC tttc_3 (
    .vin(sdr_1_h2), .vout(tttc_3_vout[2]), .hin(sdr_1_v2), .hout(tttc_1_hout[2]), .L0(tttc_3_l0),
    .L1(tttc_3_l1), .L2(tttc_3_l2), .L3(tttc_3_l3), .btn(button_3_out));
  DotMatrix #(.inputtype("row"), .matrixcols(4), .matrixrows(4)) dotmatrix_4 (
    .row0(tttc_3_l0), .row1(tttc_3_l1), .row2(tttc_3_l2), .row3(tttc_3_l3));
  Button button_3 (.out(button_3_out));
  Pull_Resistor pull_resistor_1 (.node({cdm_8_mark5_1_addr, I_Oadr}));
  DotMatrix #(.inputtype("row"), .matrixcols(4), .matrixrows(4)) dotmatrix_5 (
    .row0(tttc_4_l0), .row1(tttc_4_l1), .row2(tttc_4_l2), .row3(tttc_4_l3));
  TTTC tttc_4 (
    .vin(sdr_1_h0), .vout(tttc_1_vout[2]), .hin(sdr_1_v1), .hout(tttc_4_hout[2]), .L0(tttc_4_l0),
    .L1(tttc_4_l1), .L2(tttc_4_l2), .L3(tttc_4_l3), .btn(button_4_out));
  Button button_4 (.out(button_4_out));
  DotMatrix #(.inputtype("row"), .matrixcols(4), .matrixrows(4)) dotmatrix_6 (
    .row0(tttc_5_l0), .row1(tttc_5_l1), .row2(tttc_5_l2), .row3(tttc_5_l3));
  TTTC tttc_5 (
    .vin(sdr_1_h1), .vout(tttc_2_vout[2]), .hin(sdr_1_v1), .hout(tttc_4_hout[2]), .L0(tttc_5_l0),
    .L1(tttc_5_l1), .L2(tttc_5_l2), .L3(tttc_5_l3), .btn(button_5_out));
  Button button_5 (.out(button_5_out));
  TTTC tttc_6 (
    .vin(sdr_1_h2), .vout(tttc_3_vout[2]), .hin(sdr_1_v1), .hout(tttc_4_hout[2]), .L0(tttc_6_l0),
    .L1(tttc_6_l1), .L2(tttc_6_l2), .L3(tttc_6_l3), .btn(button_6_out));
  DotMatrix #(.inputtype("row"), .matrixcols(4), .matrixrows(4)) dotmatrix_7 (
    .row0(tttc_6_l0), .row1(tttc_6_l1), .row2(tttc_6_l2), .row3(tttc_6_l3));
  Button button_6 (.out(button_6_out));
  RAM ram_1 (.addr({cdm_8_mark5_1_addr, I_Oadr}), .data(I_Odat), .sel(RAM), .clk(Cl), .ld(In_out_prime));  // open: clr
  ROM rom_1 (.addr({cdm_8_mark5_1_addr, I_Oadr}), .data(I_Odat), .sel(code));
  TTTC tttc_7 (
    .vin(sdr_1_h0), .vout(tttc_1_vout[2]), .hin(sdr_1_v0), .hout(tttc_7_hout[2]), .L0(tttc_7_l0),
    .L1(tttc_7_l1), .L2(tttc_7_l2), .L3(tttc_7_l3), .btn(button_7_out));
  DotMatrix #(.inputtype("row"), .matrixcols(4), .matrixrows(4)) dotmatrix_8 (
    .row0(tttc_7_l0), .row1(tttc_7_l1), .row2(tttc_7_l2), .row3(tttc_7_l3));
  Button button_7 (.out(button_7_out));
  TTTC tttc_8 (
    .vin(sdr_1_h1), .vout(tttc_2_vout[2]), .hin(sdr_1_v0), .hout(tttc_7_hout[2]), .L0(tttc_8_l0),
    .L1(tttc_8_l1), .L2(tttc_8_l2), .L3(tttc_8_l3), .btn(button_8_out));
  DotMatrix #(.inputtype("row"), .matrixcols(4), .matrixrows(4)) dotmatrix_9 (
    .row0(tttc_8_l0), .row1(tttc_8_l1), .row2(tttc_8_l2), .row3(tttc_8_l3));
  Button button_8 (.out(button_8_out));
  TTTC tttc_9 (
    .vin(sdr_1_h2), .vout(tttc_3_vout[2]), .hin(sdr_1_v0), .hout(tttc_7_hout[2]), .L0(tttc_9_l0),
    .L1(tttc_9_l1), .L2(tttc_9_l2), .L3(tttc_9_l3), .btn(button_9_out));
  DotMatrix #(.inputtype("row"), .matrixcols(4), .matrixrows(4)) dotmatrix_10 (
    .row0(tttc_9_l0), .row1(tttc_9_l1), .row2(tttc_9_l2), .row3(tttc_9_l3));
  Button button_9 (.out(button_9_out));
  assign I_Odat = decoder_2_out1 ? {4'b0000, BPC_out_7} : 8'bz;  // Controlled_Buffer controlled_buffer_3
  BPC BPC (
    ._00(tttc_1_vout[2]), ._01(tttc_2_vout[2]), ._10(tttc_3_vout[2]), .out_7(BPC_out_7),
    ._00_2(tttc_1_hout[2]), ._01_2(tttc_4_hout[2]), ._10_2(tttc_7_hout[2]));
  // Probe on BPC_out_7

  // Other names for the same wires on the sheet: rd_wr_prime = In_out_prime

  // Notes on the sheet:
  //   contents of rom_1 (hex, n*v repeats v):
  //   d2 3 b9 5 e5 9 b9 ee 3 b4 0 e0 f ee 0 d0 2 a4 75 95 95 11 a9 d6 3f 0 e1 2d d6 37 d1 1 a1 70 94 94 11
  //   a9 d6 3f 0 e1 2d ee 0 d1 3 90 90 90 d2 3c 58 a4 d4 c1 c2 c3 d1 7 b4 ee 4c c1 c2 c3 d1 3 b4 4*98 44
  //   ee 4c c7 c6 c5 d7
endmodule

module TTTC (
  input  [1:0] vin,
  input  [1:0] hin,
  input  btn,
  output [3:0] L0,
  output [3:0] L1,
  output vout,
  output [3:0] L2,
  output [3:0] L3,
  output hout
);

  wire and_1_out;
  wire [1:0] sym_reg_q;

  Transistor #(.\type ("n"), .gate("br")) transistor_1 (.in(1'b1), .out(hout), .gate(btn));
  and and_1 (and_1_out, vin[1], hin[1]);
  Register #(.width(2)) sym_reg (.D({hin[0], vin[0]}), .en(and_1_out), .Q(sym_reg_q), .clk(and_1_out));  // open: clr
  ROM #(.addrWidth(2), .dataWidth(16)) rom_1 (.addr(sym_reg_q), .data({L3, L2, L1, L0}));  // open: sel

  assign vout = hout;

  // Notes on the sheet:
  //   contents of rom_1 (hex, n*v repeats v):
  //   0 f99f 9429
endmodule

module SDR (
  input  [3:0] x__y,
  input  clock,
  input  [1:0] ID,
  output [1:0] h0,
  output [1:0] h1,
  output [1:0] h2,
  output [1:0] v2,
  output [1:0] v1,
  output [1:0] v0
);

  wire decoder_1_out0, decoder_1_out1, decoder_1_out2, decoder_2_out0, decoder_2_out1, decoder_2_out2;

  Decoder #(.select(2), .enable("false")) decoder_1 (
    .out0(decoder_1_out0), .out1(decoder_1_out1), .out2(decoder_1_out2), .sel(x__y[1:0]));  // open: out3
  Decoder #(.select(2), .enable("false")) decoder_2 (
    .out0(decoder_2_out0), .out1(decoder_2_out1), .out2(decoder_2_out2), .sel(x__y[3:2]));  // open: out3
  assign h0 = decoder_1_out0 ? {clock, ID[0]} : 2'bz;  // Controlled_Buffer controlled_buffer_1
  assign h1 = decoder_1_out1 ? {clock, ID[0]} : 2'bz;  // Controlled_Buffer controlled_buffer_2
  assign h2 = decoder_1_out2 ? {clock, ID[0]} : 2'bz;  // Controlled_Buffer controlled_buffer_3
  assign v2 = decoder_2_out0 ? {clock, ID[1]} : 2'bz;  // Controlled_Buffer controlled_buffer_4
  assign v1 = decoder_2_out1 ? {clock, ID[1]} : 2'bz;  // Controlled_Buffer controlled_buffer_5
  assign v0 = decoder_2_out2 ? {clock, ID[1]} : 2'bz;  // Controlled_Buffer controlled_buffer_6

  // Notes on the sheet:
  //   H0.split(0) = if xcoord is 0b00 then symID.split(0) else float
  //   H0.split(1) = if xcoord is 0b00 then clock else float
  //   H1.split(0) = if xcoord is 0b01 then symID.split(0) else float
  //   H1.split(1) = if xcoord is 0b01 then clock else float
  //   H2.split(0) = if xcoord is 0b10 then symID.split(0) else float
  //   H2.split(1) = if xcoord is 0b10 then clock else float
  //   V0.split(0) = if ycoord is 0b00 then symID.split(1) else float
  //   V0.split(1) = if ycoord is 0b00 then clock else float
  //   V1.split(0) = if ycoord is 0b01 then symID.split(1) else float
  //   V1.split(1) = if ycoord is 0b01 then clock else float
  //   V2.split(0) = if ycoord is 0b10 then symID.split(1) else float
  //   V2.split(1) = if ycoord is 0b10 then clock else float
endmodule

module BPC (
  input  _00,
  input  _01,
  input  _10,
  input  _00_2,
  input  _01_2,
  input  _10_2,
  output [3:0] out_7
);

  wire not_1_out, or_1_out, transistor_1_out, transistor_4_out;
  wire [3:0] controlled_inverter_1_out;

  Transistor #(.\type ("n")) transistor_1 (.in(1'b0), .out(transistor_1_out), .gate(_00));
  Transistor #(.\type ("n")) transistor_2 (.in(1'b0), .out(transistor_1_out), .gate(_10));
  Transistor #(.\type ("n")) transistor_3 (.in(1'b0), .out(transistor_1_out), .gate(_01));
  Pull_Resistor #(.pull(1)) pull_resistor_1 (.node(transistor_1_out));
  or or_1 (or_1_out, transistor_4_out, transistor_1_out);
  Pull_Resistor pull_resistor_2 (.node(_00));
  Pull_Resistor pull_resistor_3 (.node(_10));
  Pull_Resistor pull_resistor_4 (.node(_01));
  not not_1 (not_1_out, or_1_out);
  assign controlled_inverter_1_out[0] = _00 ? ~_00 : 1'bz;  // Controlled_Inverter controlled_inverter_1
  assign controlled_inverter_1_out[1] = _00 ? ~_00 : 1'bz;  // Controlled_Inverter controlled_inverter_2
  assign controlled_inverter_1_out[0] = _10 ? ~_10 : 1'bz;  // Controlled_Inverter controlled_inverter_3
  assign controlled_inverter_1_out[1] = _10 ? _10 : 1'bz;  // Controlled_Buffer controlled_buffer_1
  assign controlled_inverter_1_out[1] = _01 ? ~_01 : 1'bz;  // Controlled_Inverter controlled_inverter_4
  assign controlled_inverter_1_out[0] = _01 ? _01 : 1'bz;  // Controlled_Buffer controlled_buffer_2
  assign controlled_inverter_1_out[3] = _00_2 ? ~_00_2 : 1'bz;  // Controlled_Inverter controlled_inverter_5
  assign controlled_inverter_1_out[2] = _00_2 ? ~_00_2 : 1'bz;  // Controlled_Inverter controlled_inverter_6
  Pull_Resistor pull_resistor_5 (.node(_00_2));
  Transistor #(.\type ("n")) transistor_4 (.in(1'b0), .out(transistor_4_out), .gate(_00_2));
  assign controlled_inverter_1_out[2] = _10_2 ? ~_10_2 : 1'bz;  // Controlled_Inverter controlled_inverter_7
  assign controlled_inverter_1_out[3] = _10_2 ? _10_2 : 1'bz;  // Controlled_Buffer controlled_buffer_3
  Transistor #(.\type ("n")) transistor_5 (.in(1'b0), .out(transistor_4_out), .gate(_01_2));
  assign controlled_inverter_1_out[3] = _01_2 ? ~_01_2 : 1'bz;  // Controlled_Inverter controlled_inverter_8
  Pull_Resistor pull_resistor_6 (.node(_01_2));
  Pull_Resistor pull_resistor_7 (.node(_10_2));
  Pull_Resistor #(.pull(1)) pull_resistor_8 (.node(transistor_4_out));
  Transistor #(.\type ("n")) transistor_6 (.in(1'b0), .out(transistor_4_out), .gate(_10_2));
  assign controlled_inverter_1_out[2] = _01_2 ? _01_2 : 1'bz;  // Controlled_Buffer controlled_buffer_4
  // Probe on controlled_inverter_1_out
  Register #(.width(4)) register_1 (.D(controlled_inverter_1_out), .en(1'b1), .Q(out_7), .clk(not_1_out));  // open: clr
endmodule

module GSDD (
  input  [1:0] _00___lose__10___win__11___draw,
  output [3:0] bus_0,
  output [3:0] bus_0_2,
  output [3:0] bus_0_3,
  output [3:0] bus_0_4
);

  ROM #(.addrWidth(2), .dataWidth(16)) rom_1 (
    .addr(_00___lose__10___win__11___draw), .data({bus_0, bus_0_2, bus_0_3, bus_0_4}));  // open: sel
  DotMatrix #(.matrixcols(4), .matrixrows(4)) dotmatrix_1 (
    .col0(bus_0), .col1(bus_0_2), .col2(bus_0_3), .col3(bus_0_4));

  // Notes on the sheet:
  //   contents of rom_1 (hex, n*v repeats v):
  //   6996 9249 0 ffff
endmodule
